# Fritzing sketch stripboard (saved by Fritzing 0.9.2b)
stripboards: 1

parts:
  J1 = female pin header, 4 pins [form="♀ (female)"]
  J2 = male pin header, 2 pins [form="♂ (male)"]
  J3 = male pin header, 3 pins [form="♂ (male)"]
  R1 = Resistor [tolerance=±5% resistance=10k package=THT]
  R2 = Resistor [tolerance=±5% resistance=10k package=THT]
  J5 = male pin header, 2 pins [form="♂ (male)"]
  J4 = male pin header, 2 pins [form="♂ (male)"]
  Raspberry_Pi1 = Raspberry Pi 2
  RE1 = Rotary Encoder [package=THT]
  J6 = male pin header, 6 pins [form="♂ (male)"]
  J7 = male pin header, 2 pins [form="♂ (male)"]
  J8 = Power Jack [package=power_jack_slot]
  J9 = male pin header, 2 pins [form="♂ (male)"]

nets:
  N1: J1.pin1, J8.GND, J9.pin2
  N2: J1.pin2, J2.pin1, J6.pin2, J8.PWR, J9.pin1
  N3: J1.pin3, J3.pin1, J3.pin2, J3.pin3, Raspberry_Pi1.GND, RE1.EncoderPinC, J6.pin5
  N4: J1.pin4, R1.Pin_1, R2.Pin_1
  N5: J2.pin2, R2.Pin_0, J5.pin2, J4.pin2, Raspberry_Pi1.GPIO17, RE1.EncoderPinA, J7.pin1
  N6: R1.Pin_0, J5.pin1, J4.pin1, Raspberry_Pi1.GPIO18, RE1.EncoderPinB
  N7: Raspberry_Pi1.GPIO4, J7.pin2
  N8: Raspberry_Pi1.GPIO22, Raspberry_Pi1.GPIO10, J6.pin6
  N9: Raspberry_Pi1.GPIO24, J6.pin3
  N10: Raspberry_Pi1.GPIO23, J6.pin4

notes:
  5V
  12V
  GND
  Nixie Driver
  Rotary Encoder
  Embedded Push Switch
  Kosbo DC/DC
  PoE power in
  12-5 DC/DC
  RPi power
